// Logisim project CPU_8bits.circ as structural Verilog: 4 circuits, main circuit main
module main (
  input  [3:0] OP,
  input  INTQ,
  input  ZF,
  input  CF,
  input  CLK_T1,
  input  RST,
  input  CLK_T4
);

  wire ALU_BUS, CS_RAM, CS_ROM, LDAR1, LDAR2, LDDR1, LDDR2, LDER, LDIR, LDPC, LDR4, M4, PC_1, PC_ADD, R_RAM,
       RF_BUS, W_RAM, W_RF;
  wire [1:0] WRD;
  wire [3:0] A, ALU_OP, OP_t;
  wire [5:0] next_uA, uA;
  wire [7:0] alu_8bit_xmx077_1_out_4, AR1_out_5, bit_extender_1_out, controlled_buffer_1_out,
       controlled_buffer_3_out, DR1_out_5, DR2_out_5, dr_1_out_5, ER_out_5, main_1_a_out, main_1_b_out,
       main_3_pc_out, multiplexer_1_out, pc_add_1_s_out, PreData, R4_out_5, rom_1_data;

  DR DR2 (.in_1(main_1_a_out), .LDDR(LDDR1), .out_5(DR2_out_5), .CLEAR(RST));  // open: CLK
  ALU_8bit_xmx077 alu_8bit_xmx077_1 (
    .A(DR2_out_5), .B(DR1_out_5), .in_3(ALU_OP), .out_4(alu_8bit_xmx077_1_out_4));  // open: out_5, out_6, out_7
  RF_4_main main_1 (
    .D_in(ER_out_5), .A_out(main_1_a_out), .RS(A[3:2]), .B_out(main_1_b_out), .RD(A[1:0]), .reset(RST),
    .Write(W_RF), .WRD(WRD));  // open: clk, R1_o, R0_o, R3_o, R2_o
  DR ER (.in_1(controlled_buffer_1_out), .LDDR(LDER), .out_5(ER_out_5), .CLEAR(RST));  // open: CLK
  assign controlled_buffer_1_out = ALU_BUS ? alu_8bit_xmx077_1_out_4 : 8'bz;  // Controlled_Buffer controlled_buffer_1
  DR DR1 (.in_1(main_1_b_out), .LDDR(LDDR2), .out_5(DR1_out_5), .CLEAR(RST));  // open: CLK
  assign controlled_buffer_1_out = RF_BUS ? main_1_b_out : 8'bz;  // Controlled_Buffer controlled_buffer_2
  uC uc_1 (
    .INTQ(INTQ), .ZF(ZF),
    .uOP_signal({LDR4, LDDR2, LDDR1, RF_BUS, ALU_BUS, LDER, M4, PC_ADD, LDIR, LDPC, PC_1, CS_ROM, LDAR2, LDAR1, R_RAM, W_RAM, CS_RAM, W_RF, ALU_OP}),
    .CF(CF), .OP(OP), .clk_T1(CLK_T1), .reset(RST), .clk_T4(CLK_T4), .Current_UA(uA), .next_uA(next_uA));  // open: Pre_Data, out_10, out_11, out_12, out_13
  RAM_8bits_main main_2 (
    .Add_in(AR1_out_5), .D_in(controlled_buffer_3_out), .D_out(controlled_buffer_1_out), .Write(W_RAM),
    .cs(CS_RAM), .Read(R_RAM), .CLR(RST));  // open: clk
  assign controlled_buffer_3_out = W_RAM ? controlled_buffer_1_out : 8'bz;  // Controlled_Buffer controlled_buffer_3
  DR AR1 (.in_1(controlled_buffer_1_out), .LDDR(LDAR1), .out_5(AR1_out_5), .CLEAR(RST));  // open: CLK
  DR dr_1 (.in_1(main_3_pc_out), .LDDR(LDAR2), .out_5(dr_1_out_5), .CLEAR(RST));  // open: CLK
  PC_Register3_main main_3 (
    .reset(RST), .PC_in(pc_add_1_s_out), .Preset_data(PreData), .PC_out(main_3_pc_out), .PC_1(PC_1),
    .LDPC(LDPC));  // open: clk_T4
  PC_ADD pc_add_1 (.Din_1(R4_out_5), .Din_2(main_3_pc_out), .PC_ADD(PC_ADD), .S_out(pc_add_1_s_out));
  DR R4 (.in_1(multiplexer_1_out), .LDDR(LDR4), .out_5(R4_out_5), .CLEAR(RST));  // open: CLK
  Multiplexer #(.width(8), .enable("false")) multiplexer_1 (
    .in0(controlled_buffer_1_out), .in1(bit_extender_1_out), .out(multiplexer_1_out), .sel(M4));
  ROM rom_1 (.addr(dr_1_out_5), .data(rom_1_data), .sel(CS_ROM));
  assign bit_extender_1_out = {{4{1'b0}}, A};  // Bit_Extender bit_extender_1
  DR IR (.in_1(rom_1_data), .LDDR(LDIR), .out_5({OP_t, A}), .CLEAR(RST));  // open: CLK

  // Other names for the same wires on the sheet: RD[1:0] = A[1:0]; RS[1:0] = A[3:2]; reset = RST
endmodule

module DR (
  input  [7:0] in_1,
  input  LDDR,
  input  CLK,
  input  CLEAR,
  output [7:0] out_5
);

  Register register_1 (.D(in_1), .en(LDDR), .Q(out_5), .clk(CLK), .clr(CLEAR));
endmodule

module PC_ADD (
  input  [7:0] Din_1,
  input  [7:0] Din_2,
  input  PC_ADD,
  output [7:0] S_out
);

  wire [7:0] fa_8bits_unsigned_xmx077_1_s_a;

  FA_8bits_unsigned_xmx077 fa_8bits_unsigned_xmx077_1 (
    .A(Din_1), .B(Din_2), .S_A(fa_8bits_unsigned_xmx077_1_s_a));  // open: out_4, out_5
  Multiplexer #(.width(8), .enable("false")) multiplexer_1 (
    .in0(Din_1), .in1(fa_8bits_unsigned_xmx077_1_s_a), .out(S_out), .sel(PC_ADD));
endmodule

module uC (
  input  INTQ,
  input  ZF,
  input  CF,
  input  [3:0] OP,
  input  clk_T1,
  input  reset,
  input  clk_T4,
  input  [7:0] Pre_Data,
  output [21:0] uOP_signal,
  output out_10,
  output out_11,
  output out_12,
  output out_13,
  output [5:0] next_uA,
  output [5:0] Current_UA
);

  wire and_1_out, and_2_out, and_3_out, and_4_out, and_5_out, and_6_out, and_7_out, and_8_out, and_9_out,
       and_10_out, and_11_out, and_12_out, nor_1_out, not_1_out, not_2_out, not_3_out;
  wire [5:0] register_1_q;
  wire [7:0] bit_extender_1_out, main_1_q_out;
  wire [31:0] rom_1_data;

  ROM #(.addrWidth(6), .dataWidth(32)) rom_1 (.addr(Current_UA), .data(rom_1_data), .sel(1'b1));
  Register #(.width(32)) register_1 (
    .D(rom_1_data), .en(1'b1),
    .Q({uOP_signal, out_10, out_11, out_12, out_13, register_1_q[5], next_uA[4], register_1_q[3:0]}),
    .clk(clk_T1), .clr(reset));
  not not_1 (not_1_out, ZF);
  nor nor_1 (nor_1_out, out_10, out_12, out_13);
  not not_2 (not_2_out, out_11);
  and and_1 (and_1_out, not_1_out, out_10);
  and and_2 (and_2_out, CF, out_13);
  and and_3 (and_3_out, nor_1_out, register_1_q[5]);
  and and_4 (and_4_out, out_12, INTQ);
  and and_5 (and_5_out, not_2_out, register_1_q[0]);
  and and_6 (and_6_out, out_11, OP[0]);
  and and_7 (and_7_out, not_2_out, register_1_q[1]);
  and and_8 (and_8_out, out_11, OP[1]);
  and and_9 (and_9_out, not_2_out, register_1_q[2]);
  and and_10 (and_10_out, out_11, OP[2]);
  and and_11 (and_11_out, not_2_out, register_1_q[3]);
  and and_12 (and_12_out, out_11, OP[3]);
  or or_1 (next_uA[5], and_1_out, and_2_out, and_3_out, and_4_out);
  or or_2 (next_uA[0], and_5_out, and_6_out);
  or or_3 (next_uA[1], and_7_out, and_8_out);
  or or_4 (next_uA[2], and_9_out, and_10_out);
  or or_5 (next_uA[3], and_11_out, and_12_out);
  assign bit_extender_1_out = {{2{1'b0}}, next_uA};  // Bit_Extender bit_extender_1
  uAddressR_main main_1 (
    .clk_T4(clk_T4), .reset(reset), .D_in(bit_extender_1_out), .Preset_data(Pre_Data), .Q_out(main_1_q_out),
    .Load(not_3_out));
  not not_3 (not_3_out, reset);
  Bit_Extender #(.out_width(6)) bit_extender_2 (.in(main_1_q_out), .out(Current_UA));

  // Other names for the same wires on the sheet: P0 = out_13; P1 = out_12; P2 = out_11; P3 = out_10; T1 = clk_T1;
  //   T4 = clk_T4; uA_in[5:0] = Current_UA

  // Notes on the sheet:
  //   contents of rom_1 (hex, n*v repeats v):
  //   0 1 2 3 4 b80010 6 7 8 9 a b c d e f 6000003b 6000003a 60000039 60000038 5004002b 10040035 60000034
  //   60000033 9040000f 4f 20f1a 1b 1c 1d 1e 1f 20 21 22 23 24 25 26 27 28 29 400f 801800f 2c 2d 2e 2f
  //   c000c2a c00102a 32 c00182a c001c2a 402802a 36 37 c00202a c00142a c00042a c00082a 3c 3d 3e 3f
endmodule
